# Fritzing sketch WIFIesp8266 (saved by Fritzing 0.9.3b)
breadboards: 1

parts:
  R1 = Resistor [tolerance=±5% resistance=220 package=THT]
  LED1 = LED - 5mm [color="Red (633nm)" package="5 mm [THT]"]
  Part1 = Arduino Uno (Rev3)
  Adafruit_HUZZAH_ESP8266_Breakout1 = Adafruit HUZZAH ESP8266 Breakout [part_number=2471]

nets:
  N1: R1.Pin_0, LED1.anode
  GND: R1.Pin_1, Part1.GND, Adafruit_HUZZAH_ESP8266_Breakout1.GND, Adafruit_HUZZAH_ESP8266_Breakout1.VBat
  N2: Part1.D11_PWM/MOSI, Part1.3V3, Adafruit_HUZZAH_ESP8266_Breakout1.EN, Adafruit_HUZZAH_ESP8266_Breakout1.3V
  N3: Part1.D2, Adafruit_HUZZAH_ESP8266_Breakout1.TX
  N4: Part1.D3_PWM, Adafruit_HUZZAH_ESP8266_Breakout1.RX
